# Fritzing sketch circuit (saved by Fritzing 0.5.2b)
breadboards: 1

parts:
  Arduino1 = Arduino
  LED1 = RGB LED - (4 legs) [package="5 mm [THT]"]
  R3 = Resistor [resistance=220 package=THT]
  R2 = Resistor [resistance=220 package=THT]
  R1 = Resistor [resistance=220 package=THT]

nets:
  N1: Arduino1.D6, R3.Pin_0
  N2: Arduino1.D5, R2.Pin_0
  N3: Arduino1.D3, R1.Pin_0
  N4: Arduino1.+5V, LED1.common_anode
  N5: LED1.red_cathode, R1.Pin_1
  N6: LED1.green_cathode, R2.Pin_1
  N7: LED1.blue_cathode, R3.Pin_1
